# Fritzing sketch DOG_Schema (saved by Fritzing 1.0.1rc)

parts:
  Ultrasone = HC-SR04 Ultrasonic Distance Sensor
  Ultrasone_2 = HC-SR04 Ultrasonic Distance Sensor
  8x8_LED_Modul_mit_MAX1 = 8x8 LED Modul mit MAX7219 [package=THT]
  8x8_LED_Modul_mit_MAX2 = 8x8 LED Modul mit MAX7219 [package=THT]
  A1 = Jetson Nano
  Part1 = Adafruit MAX98357A I2S 3W Class D Amplifier [part_number="Adafruit #3006"]
  SPKR1 = Loudspeaker
  Fusion_IMU = Adafruit BNO055 STEMMA QT [part_number="Adafruit #4646"]
  A3 = ESP32 DevKitc V4
  Flow_Sensor_2 = Generic female header - 7 pins [form="♀ (female)" package=THT]
  Flow_Sensor_1 = Generic female header - 7 pins [form="♀ (female)" package=THT]
  U1 = TRANSCHIPTC5747 [package=camera_sfv24r-2st_2]  # not connected
  Part2 = Arduino Uno (Rev3) - ICSP
  J2 = Dagu DGServo 9g header connector (female) [package=THT]

nets:
  VCC: Ultrasone.VCC, Ultrasone_2.VCC, 8x8_LED_Modul_mit_MAX2.VCC_Eingang, A3.Pin_19
  N1: Ultrasone.TRIG, A3.Pin_12
  N2: Ultrasone.ECHO, A3.Pin_11
  GND: Ultrasone.GND, Ultrasone_2.GND, 8x8_LED_Modul_mit_MAX2.GND_Eingang, Fusion_IMU.GND, A3.Pin_14, A3.Pin_32, A3.Pin_38, Flow_Sensor_2.GND, Flow_Sensor_1.GND
  N3: Ultrasone_2.TRIG, A3.Pin_10
  N4: Ultrasone_2.ECHO, A3.Pin_9
  N5: 8x8_LED_Modul_mit_MAX1.VCC_Eingang, 8x8_LED_Modul_mit_MAX2.VCC_Ausgang
  N6: 8x8_LED_Modul_mit_MAX1.GND_Eingang, 8x8_LED_Modul_mit_MAX2.GND_Ausgang
  N7: 8x8_LED_Modul_mit_MAX1.DIN_Eingang, 8x8_LED_Modul_mit_MAX2.DOUT_Ausgang
  N8: 8x8_LED_Modul_mit_MAX1.CS_Eingang, 8x8_LED_Modul_mit_MAX2.CS_Ausgang
  N9: 8x8_LED_Modul_mit_MAX1.CLK_Eingang, 8x8_LED_Modul_mit_MAX2.CLK_Ausgang
  N10: 8x8_LED_Modul_mit_MAX2.DIN_Eingang, A3.Pin_37, Flow_Sensor_2.MOSI, Flow_Sensor_1.MOSI
  N11: 8x8_LED_Modul_mit_MAX2.CS_Eingang, A3.Pin_27
  N12: 8x8_LED_Modul_mit_MAX2.CLK_Eingang, A3.Pin_30, Flow_Sensor_2.SCK, Flow_Sensor_1.SCK
  N13: A1.3V3, Part1.DIN
  GND_2: A1.GND, Part1.VIN, Part1.LRCLK
  N14: A1.29, Part1.BCLK
  N15: A1.35, A1.37, Part1.GND
  N16: Part1.VO-, SPKR1.pin1
  N17: Part1.VO+, SPKR1.pin2
  VCC_2: Fusion_IMU.VCC, Fusion_IMU.3.3V, A3.Pin_1, Flow_Sensor_2.3-5V, Flow_Sensor_1.3-5V
  N18: Fusion_IMU.SDA, Fusion_IMU.RESET, A3.Pin_33
  N19: Fusion_IMU.SCL, A3.Pin_36
  N20: A3.Pin_28, Flow_Sensor_2.CS
  N21: A3.Pin_29, Flow_Sensor_1.CS
  N22: A3.Pin_31, Flow_Sensor_2.MISO, Flow_Sensor_1.MISO
  N23: Part2.D0/RX, J2.Vcc
  N24: Part2.D1/TX, J2.pulse
  GND_3: Part2.GND, J2.gnd

custom parts:
  Adafruit MAX98357A I2S 3W Class D Amplifier: Listen to this good news - we now have an all in one digital audio amp breakout board that works incredibly well with the Raspberry Pi! If you're looking for an easy and low cost way to get you digital sound files bumpin' then the MAX08357 I2S Amp Breakout is for you. It takes standard I2S digital audio input and, not only decodes it into analog, but also amplifies it directly into a speaker.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
  Adafruit BNO055 STEMMA QT: If you've ever ordered and wire up a 9-DOF sensor, chances are you've also realized the challenge of turning the sensor data from an accelerometer, gyroscope, and magnetometer into actual "3D space orientation"! Orientation is a hard problem to solve. The sensor fusion algorithms (the secret sauce that blends accelerometer, magnetometer, and gyroscope data into stable three-axis orientation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
  ESP32 DevKitc V4: ESP32-DevKitC board with ESP32-WROOM-32 module. ESP32-DevKitC V4 is a small-sized ESP32-based development board produced by Espressif. Most of the pins on the ESP module are broken out to the pin headers on the board. The pins D0, D1, D2, D3, CMD and CLK are used internally for communication between ESP32 and SPI flash memory. They are grouped on both sides near the USB connector. Avoid using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
  Generic female header - 7 pins: Generic female header
